# Fritzing sketch klonk (saved by Fritzing 0.9.2b)
breadboards: 1

parts:
  Pro_Micro1 = Pro Micro
  Bauteil1 = RFID-RC522-v2
  D1 = Rectifier Diode [part_number=1N4001 package="300 mil [THT]"]
  D2 = Rectifier Diode [part_number=1N4001 package="300 mil [THT]"]
  R1 = Resistor [tolerance=±5% resistance=220 package=THT]
  LED1 = LED - 5mm [color="Red (633nm)" package="5 mm [THT]"]
  S1 = Pushbutton [package=THT]
  R2 = Resistor [tolerance=±5% resistance=220 package=THT]

nets:
  N1: Pro_Micro1.D2, Bauteil1.SDA
  N2: Pro_Micro1.D3, Bauteil1.RST
  N3: Pro_Micro1.D4, S1.leg1
  N4: Pro_Micro1.D5, R1.Pin_1
  N5: Pro_Micro1.D16/MOSI, Bauteil1.MOSI
  N6: Pro_Micro1.D14/MISO, Bauteil1.MISO
  N7: Pro_Micro1.D15/SCLK, Bauteil1.SCK
  N8: Pro_Micro1.VCC, D1.anode
  GND: Pro_Micro1.GND, Bauteil1.GND, LED1.cathode, R2.Pin_0
  N9: Bauteil1.3.3V, D2.cathode
  N10: D1.cathode, D2.anode
  N11: R1.Pin_0, LED1.anode
  N12: S1.leg0, R2.Pin_1

custom parts:
  Pro Micro: The SparkFun Pro Micro is a complete USB-based microcontoller development system, in a very small footprint, capable of implementing many types of projects. All programming can be done via the USB port.
  RFID-RC522-v2: A simple China made RFID-RC522 Reader; do check the pin labels, as this is a MFRC522 based clone.
